# Fritzing sketch Circuit Diagram (saved by Fritzing 0.8.7b)
breadboards: 1

parts:
  Part1 = Arduino Uno (Rev3)
  R1 = PHOTOCELL [package=photocell-kit]
  LED1 = LED - 5mm [color="Red (633nm)" package="5 mm [THT]"]
  R2 = Resistor [package="2010 [SMD]"]
  R3 = Resistor [package="2010 [SMD]"]

nets:
  N1: Part1.A0, R3.Pin_0
  N2: Part1.D11_PWM/MOSI, R2.Pin_1
  N3: Part1.GND, R1.P$1, LED1.cathode, R3.Pin_1
  N4: Part1.5V, R1.P$2
  N5: LED1.anode, R2.Pin_0
