# Fritzing sketch Seven Segment wiring (saved by Fritzing 0.8.7b)
breadboards: 1

parts:
  Part1 = Arduino Uno (Rev3)
  DI1 = 7-Segment LED Display [package=THT]
  R1 = Resistor [tolerance=±5% resistance=220 package=THT]
  R2 = Resistor [tolerance=±5% resistance=220 package=THT]
  R3 = Resistor [tolerance=±5% resistance=220 package=THT]
  R4 = Resistor [tolerance=±5% resistance=220 package=THT]
  R5 = Resistor [tolerance=±5% resistance=220 package=THT]
  R6 = Resistor [tolerance=±5% resistance=220 package=THT]
  R7 = Resistor [tolerance=±5% resistance=220 package=THT]

nets:
  N1: Part1.D8, R4.Pin_0
  N2: Part1.D2, R1.Pin_1
  N3: Part1.D3_PWM, R2.Pin_1
  N4: Part1.D4, R7.Pin_1
  N5: Part1.D5_PWM, R6.Pin_0
  N6: Part1.D6_PWM, R5.Pin_0
  N7: Part1.D7, R3.Pin_0
  N8: Part1.GND, DI1.commAnode#7
  N9: DI1.cathodeE, R5.Pin_1
  N10: DI1.cathodeD, R6.Pin_1
  N11: DI1.cathodeC, R7.Pin_0
  N12: DI1.cathodeB, R2.Pin_0
  N13: DI1.cathodeA, R1.Pin_0
  N14: DI1.cathodeF, R3.Pin_1
  N15: DI1.cathodeG, R4.Pin_1
