# Fritzing sketch LCD circuit (saved by Fritzing 0.8.7b)

parts:
  Part1 = Arduino Uno (Rev3)
  U1 = LCD-16X2 [package=lcd-16x2]
  R1 = Resistor [tolerance=±5% resistance=220 package=THT]
  R2 = Trimmer Potentiometer [maximum_resistance=10kΩ package=THT]

nets:
  N1: Part1.D8, U1.DB2
  N2: Part1.D9_PWM, U1.DB1
  N3: Part1.D10_PWM/SS, U1.DB0
  N4: Part1.D11_PWM/MOSI, U1.E
  N5: Part1.D12/MISO, U1.R_W
  N6: Part1.D13/SCK, Part1.5V, U1.VO, U1.RS, R1.Pin_0
  GND: Part1.GND, U1.VSS, U1.K
  N7: Part1.D3_PWM, U1.DB7
  N8: Part1.D4, U1.DB6
  N9: Part1.D5_PWM, U1.DB5
  N10: Part1.D6_PWM, U1.DB4
  N11: Part1.D7, U1.DB3
  N12: U1.VDD, R2.leg2
  N13: U1.A, R1.Pin_1
