# Fritzing sketch Circuit Diagram (saved by Fritzing 0.8.7b)
breadboards: 1

parts:
  Part1 = Arduino Uno (Rev3)
  LED1 = LED - 5mm [color="Red (633nm)" package="5 mm [THT]"]
  LED3 = LED - 5mm [color="Green (555nm)" package="5 mm [THT]"]
  R1 = Resistor [tolerance=±5% resistance=220 package=THT]
  R2 = Resistor [tolerance=±5% resistance=220 package=THT]
  R3 = Resistor [tolerance=±5% resistance=220 package=THT]
  LED4 = smd LED [color="Yellow (585nm)" package="1206 [SMD]"]

nets:
  N1: Part1.D12/MISO, R3.Pin_1
  N2: Part1.D13/SCK, R2.Pin_1
  N3: Part1.GND, LED1.cathode, LED3.cathode, LED4.cathode
  N4: LED1.anode, R2.Pin_0
  N5: LED3.anode, R1.Pin_0
  N6: R3.Pin_0, LED4.anode
